// Logisim project self_pipeline.circ as structural Verilog
module PC (
  input  [31:0] din__32bit
);

  wire clk, keep, rst_n;
  wire [31:0] multiplexer_1_out, pc;

  Multiplexer #(.select(1), .width(32), .disabled("Z"), .enable("false")) multiplexer_1 (
    .in0(din__32bit), .in1(32'hfffffffc), .out(multiplexer_1_out), .sel(rst_n));
  Register #(.width(32), .trigger("rising"), .Select("low")) register_1 (
    .D(multiplexer_1_out), .Q(pc), .clk(clk), .preset(keep));  // open: en, clr, cs

  // Notes on the sheet:
  //   1bit
  //   32bit
endmodule

module NPC (
);

  wire op;
  wire [31:0] npc, npc_change, pc, pc4;

  Adder #(.width(32)) adder_1 (.a(32'h4), .b(pc), .out(pc4));  // open: cin, cout
  Multiplexer #(.select(1), .width(32), .disabled("Z"), .enable("false")) multiplexer_1 (
    .in0(pc4), .in1(npc_change), .out(npc), .sel(op));

  // Notes on the sheet:
  //   32bit
  //   32bit
  //   1bit
  //   32bit
  //   32bit
endmodule

module NPC_CONTROL (
);

  wire bne_out, not_1_out, npc_op, sgn, zero;
  wire [1:0] jump;
  wire [3:0] jump_0___branch;
  wire [31:0] alu_c, npc_change, pc_imm, xor_1_out;

  assign xor_1_out = alu_c ^ 32'h1;  // XOR_Gate xor_1, 32 bits wide
  not bne (bne_out, zero);
  not not_1 (not_1_out, sgn);
  Multiplexer #(.select(2), .width(32), .disabled("Z"), .enable("false")) multiplexer_1 (
    .in1(xor_1_out), .in3(pc_imm), .out(npc_change), .sel(jump));  // open: in0, in2
  Multiplexer #(.select(4), .width(1), .disabled(0), .enable("false")) multiplexer_2 (
    .in0(zero), .in6(bne_out), .in8(sgn), .in14(not_1_out), .out(npc_op), .sel(jump_0___branch));  // open: in1, in2, in3, in4, in5, in7, in9, in10, in11, in12, in13, in15

  // Notes on the sheet:
  //   1+3bit
  //   2bit
  //   32bit
  //   32bit
  //   32bit
  //   1bit
  //   1bit
  //   beq
  //   blt
  //   bge
  //   32bit
  //   1bit
endmodule
