// Logisim project self_single_cycle.circ as structural Verilog
module PC (
  input  [31:0] din__32bit
);

  wire clk, rst_n;
  wire [31:0] multiplexer_1_out, pc;

  Multiplexer #(.select(1), .width(32), .disabled("Z"), .enable("false")) multiplexer_1 (
    .in0(din__32bit), .in1(32'hfffffffc), .out(multiplexer_1_out), .sel(rst_n));
  Register #(.width(32), .trigger("rising"), .Select("low")) register_1 (
    .D(multiplexer_1_out), .Q(pc), .clk(clk));  // open: en, clr

  // Notes on the sheet:
  //   32bit
endmodule

module NPC (
);

  wire [1:0] op;
  wire [31:0] adder_2_out, alu_c, imm, npc, pc, pc4, xor_1_out;

  assign xor_1_out = alu_c ^ 32'h1;  // XOR_Gate xor_1, 32 bits wide
  Adder #(.width(32)) adder_1 (.a(32'h4), .b(pc), .out(pc4));  // open: cin, cout
  Adder #(.width(32)) adder_2 (.a(pc), .b(imm), .out(adder_2_out));  // open: cin, cout
  Multiplexer #(.select(2), .width(32), .disabled("Z"), .enable("false")) multiplexer_1 (
    .in0(pc4), .in1(adder_2_out), .in3(xor_1_out), .out(npc), .sel(op));  // open: in2

  // Notes on the sheet:
  //   32bit
  //   32bit
  //   32bit
  //   32bit
  //   32bit
  //   2bit
endmodule

module SEXT (
);

  wire [2:0] op;
  wire [23:0] din;
  wire [31:0] bit_extender_1_out, bit_extender_3_out, bit_extender_4_out, bit_extender_5_out,
       bit_extender_6_out, ext;

  assign bit_extender_1_out = {{8{1'b0}}, din};  // Bit_Extender bit_extender_1
  assign bit_extender_1_out = {{8{1'b0}}, din};  // Bit_Extender bit_extender_2
  assign bit_extender_3_out = {{8{1'b0}}, din};  // Bit_Extender bit_extender_3
  assign bit_extender_4_out = {{8{1'b0}}, din};  // Bit_Extender bit_extender_4
  assign bit_extender_5_out = {{8{1'b0}}, din};  // Bit_Extender bit_extender_5
  assign bit_extender_6_out = {{8{1'b0}}, din};  // Bit_Extender bit_extender_6
  Multiplexer #(.select(3), .width(32), .disabled("Z"), .enable("false")) multiplexer_1 (
    .in0(bit_extender_1_out), .in1(bit_extender_1_out), .in2(bit_extender_3_out), .in3(bit_extender_4_out),
    .in4(bit_extender_5_out), .in5(bit_extender_6_out), .out(ext), .sel(op));  // open: in6, in7

  // Notes on the sheet:
  //   24bit
  //   IMM_I
  //   IMM_SHIFT
  //   IMM_S
  //   IMM_U
  //   IMM_B
  //   IMM_J
  //   3bit
  //   32bit
endmodule

module ALU (
);

  wire zero;
  wire [2:0] op;
  wire [31:0] A, adder_1_out, and_1_out, B, C, or_1_out, shifter_1_out, shifter_2_out, shifter_3_out,
       subtractor_1_out, xor_1_out;

  Adder #(.width(32)) adder_1 (.a(A), .b(B), .out(adder_1_out));  // open: cin, cout
  Subtractor #(.width(32)) subtractor_1 (.a(A), .b(B), .out(subtractor_1_out));  // open: bin, bout
  assign and_1_out = A & B;  // AND_Gate and_1, 32 bits wide
  assign or_1_out = A | B;  // OR_Gate or_1, 32 bits wide
  assign xor_1_out = A ^ B;  // XOR_Gate xor_1, 32 bits wide
  Shifter #(.width(32), .shift("ll")) shifter_1 (.in(A), .\dist (B[4:0]), .out(shifter_1_out));
  Shifter #(.width(32), .shift("lr")) shifter_2 (.in(A), .\dist (B[4:0]), .out(shifter_2_out));
  Shifter #(.width(32), .shift("ar")) shifter_3 (.in(A), .\dist (B[4:0]), .out(shifter_3_out));
  Multiplexer #(.select(3), .width(32), .disabled("Z"), .enable("false")) multiplexer_1 (
    .in0(adder_1_out), .in1(subtractor_1_out), .in2(and_1_out), .in3(or_1_out), .in4(xor_1_out),
    .in5(shifter_1_out), .in6(shifter_2_out), .in7(shifter_3_out), .out(C), .sel(op));
  Comparator #(.width(32), .mode("twosComplement")) comparator_1 (.a({32{1'b0}}), .b(C), .eq(zero));  // open: gt, lt

  // Other names for the same wires on the sheet: sgn = C[31]

  // Notes on the sheet:
  //   32bit
  //   shamt = B[4:0]
  //   ADD
  //   SUB
  //   AND
  //   OR
  //   XOR
  //   SLL
  //   SRL
  //   SRA
  //   32bit
  //   3bit
  //   32bit
  //   1bit
  //   1bit
endmodule
